# Fritzing sketch Schaltung (saved by Fritzing 0.9.3b)
circuit board: 5.82cm x 5.77cm
breadboards: 1

parts:
  WeMos_D1_Mini1 = WeMos D1 Mini
  G|24V|S = male pin header, 3 pins [form="♂ (male)"]
  V|Sig|G|G = Humidity and Temperature Sensor RHT03
  LM358 = LM 358 Dual Op-Amp [package="DIP8 [THT]"]
  4_7k = Resistor [tolerance=±5% resistance=4.7k package=THT]
  100k = Resistor [tolerance=±5% resistance=100k package=THT]
  10k = Resistor [tolerance=±5% resistance=10k package=THT]
  |> = Rectifier Diode [part_number=1N4001 package="300 mil [THT]"]
  100 = Resistor [tolerance=±5% resistance=100 package=THT]
  100nF = Ceramic Capacitor [capacitance=100nF package="100 mil [THT, multilayer]"]
  LM2574 = LM2574N-5 [package=dip08]
  22µF = Tantalum Capacitor [capacitance=22µF package="100 mil [THT, tantalum]"]
  11DQ05 = Schottky Diode [part_number=1N5817 package="300 mil [THT]"]
  V|G|SCL|SDA = male pin header, 4 pins [form="♂ (male)"]
  330µH = Inductor [inductance=330µH package="400 mil [THT]"]
  220µF = Electrolytic Capacitor [capacitance=0.22mF voltage=20V package="300 mil [THT, electrolytic]"]
  R1 = Resistor [tolerance=±5% resistance=220 package=THT]
  Q1 = NPN-Transistor [package="TO92 [THT]"]
  |>1 = Rectifier Diode [part_number=1N4001 package="300 mil [THT]"]
  R2 = Resistor [tolerance=±5% resistance=220 package=THT]
  Q2 = NPN-Transistor [package="TO92 [THT]"]
  FAN = male pin header, 2 pins [form="♂ (male)"]

nets:
  5V: WeMos_D1_Mini1.5V, V|Sig|G|G.Vcc, 4_7k.Pin_0, LM2574.FB, V|G|SCL|SDA.pin4, 330µH.pin_1, 220µF.+, FAN.pin2
  N1: WeMos_D1_Mini1.A0, LM358.connector1, 100k.Pin_0, 10k.Pin_1
  N2: WeMos_D1_Mini1.D1, Q1.B
  N3: WeMos_D1_Mini1.D3, 100.Pin_0
  N4: WeMos_D1_Mini1.D5, V|G|SCL|SDA.pin2
  N5: WeMos_D1_Mini1.D6, V|G|SCL|SDA.pin1
  N6: WeMos_D1_Mini1.D7, V|Sig|G|G.Data-signal, 4_7k.Pin_1
  N7: WeMos_D1_Mini1.D8, Q2.B
  GND: WeMos_D1_Mini1.G, G|24V|S.pin1, V|Sig|G|G.GND_1, V|Sig|G|G.GND_2, LM358.connector3, 10k.Pin_0, 100nF.1, LM2574.Sig_GND, LM2574.ON_OFF, LM2574.PWR_GND, 22µF.-, 11DQ05.anode, V|G|SCL|SDA.pin3, 220µF.-, Q1.E, R2.Pin_1, Q2.E
  N8: G|24V|S.pin2, LM358.connector7, LM2574.Vin, 22µF.+
  N9: G|24V|S.pin3, 100k.Pin_1, |>.cathode, R1.Pin_1, |>1.anode
  N10: LM358.connector0, |>.anode
  N11: LM358.connector2, 100.Pin_1, 100nF.0
  N12: LM2574.OUT, 11DQ05.cathode, 330µH.pin_0
  N13: R1.Pin_0, Q1.C
  N14: |>1.cathode, R2.Pin_0
  N15: Q2.C, FAN.pin1

notes:
  V --> 5V
  G --> GND
  SCL --> D5:GPIO14
  SDA --> D6:GPIO12
  R1 --> Controlled Pull-Down zum runterziehen auf 5V
  R2 --> Basis Pull-Down zum tunen auf 10V
  Reset und Displayreset --> nicht belegt
  Q1/Q2 --> TIP21 NPN-Transistoren
  TRQ21-Rev.2.1

custom parts:
  LM2574N-5: Schlatregler 5V
